// Logisim project dungoc.circ as structural Verilog: 1 circuit, main circuit main
module main (
  input  in_1,
  input  in_2
);

  wire and_1_out, and_2_out, and_3_out, and_4_out, and_5_out, and_6_out, and_7_out, and_8_out, and_9_out,
       and_10_out, and_11_out, and_12_out, and_13_out, and_14_out, and_15_out, and_16_out, and_17_out,
       and_18_out, and_19_out, and_20_out, and_21_out, and_22_out, and_23_out, and_24_out, and_25_out,
       and_26_out, and_27_out, and_28_out, and_29_out, and_30_out, and_31_out, and_32_out, and_33_out,
       and_34_out, and_35_out, and_36_out, and_37_out, and_38_out, and_40_out, and_42_out, and_43_out,
       and_44_out, and_45_out, and_46_out, and_47_out, and_48_out, buffer_1_out, buffer_2_out, buffer_3_out,
       buffer_4_out, buffer_5_out, buffer_6_out, buffer_7_out, buffer_8_out, buffer_9_out, buffer_10_out,
       buffer_11_out, buffer_12_out, buffer_13_out, buffer_14_out, buffer_15_out, buffer_16_out,
       buffer_17_out, buffer_18_out, buffer_19_out, buffer_20_out, d_ff_1_q, d_ff_2_q, d_ff_3_q, d_ff_4_q,
       d_ff_5_q, d_ff_6_q, d_ff_7_q, d_ff_8_q, j_k_ff_1_q, j_k_ff_1_qn, j_k_ff_2_qn, j_k_ff_3_qn,
       j_k_ff_4_qn, j_k_ff_5_qn, j_k_ff_6_qn, j_k_ff_7_qn, next_out, nor_1_out, nor_2_out, nor_3_out,
       nor_4_out, not_1_out, not_2_out, not_3_out, not_4_out, not_5_out, not_6_out, not_7_out, not_8_out,
       not_9_out, not_10_out, not_11_out, not_12_out, not_13_out, not_14_out, not_15_out, not_16_out,
       or_1_out, or_2_out, or_3_out, or_4_out, or_5_out, or_6_out, or_7_out, or_8_out, or_9_out, or_10_out,
       or_11_out, or_12_out, or_13_out, or_14_out, or_15_out, or_16_out, or_17_out, or_18_out, or_19_out,
       pause_out, play_out, prev_out, voldown_out, volup_out, xor_1_out, xor_2_out;
  wire [3:0] and_39_out, and_41_out, j_k_ff_2_q, j_k_ff_3_q;

  Button volup (.out(volup_out));
  Button voldown (.out(voldown_out));
  Button prev (.out(prev_out));
  Button next (.out(next_out));
  Button play (.out(play_out));
  Button pause (.out(pause_out));
  nor nor_1 (nor_1_out, volup_out, nor_2_out);
  nor nor_2 (nor_2_out, nor_1_out, voldown_out);
  xor xor_1 (xor_1_out, voldown_out, volup_out);
  nor nor_3 (nor_3_out, prev_out, nor_4_out);
  nor nor_4 (nor_4_out, nor_3_out, next_out);
  buf buffer_1 (buffer_1_out, buffer_2_out);
  buf buffer_2 (buffer_2_out, xor_2_out);
  xor xor_2 (xor_2_out, next_out, prev_out);
  buf buffer_3 (buffer_3_out, xor_1_out);
  buf buffer_4 (buffer_4_out, buffer_5_out);
  buf buffer_5 (buffer_5_out, buffer_3_out);
  buf buffer_6 (buffer_6_out, buffer_1_out);
  buf buffer_7 (buffer_7_out, buffer_9_out);
  buf buffer_8 (buffer_8_out, buffer_7_out);
  buf buffer_9 (buffer_9_out, buffer_6_out);
  or or_1 (or_1_out, play_out, pause_out);
  not not_1 (not_1_out, nor_1_out);
  and and_1 (and_1_out, not_1_out, nor_2_out);
  buf buffer_10 (buffer_10_out, buffer_13_out);
  buf buffer_11 (buffer_11_out, buffer_12_out);
  buf buffer_12 (buffer_12_out, buffer_10_out);
  buf buffer_13 (buffer_13_out, buffer_4_out);
  buf buffer_14 (buffer_14_out, buffer_15_out);
  buf buffer_15 (buffer_15_out, buffer_8_out);
  J_K_Flip_Flop j_k_ff_1 (
    .J(or_1_out), .K(pause_out), .clk(or_1_out), .Q(j_k_ff_1_q), .Qn(j_k_ff_1_qn));  // open: preset, reset
  and and_2 (and_2_out, nor_1_out, d_ff_2_q);
  buf buffer_16 (buffer_16_out, buffer_11_out);
  and and_3 (and_3_out, buffer_16_out, in_1);
  D_Flip_Flop d_ff_1 (.D(or_2_out), .clk(and_3_out), .Q(d_ff_1_q));  // open: Qn, preset, reset
  or or_2 (or_2_out, and_2_out, and_1_out);
  not not_2 (not_2_out, nor_3_out);
  and and_4 (and_4_out, in_1, d_ff_1_q);
  LED VOLUME1 (.in(and_4_out));
  J_K_Flip_Flop j_k_ff_2 (
    .J(1'b1), .K(1'b1), .clk(buffer_14_out), .Q(j_k_ff_2_q[0]), .Qn(j_k_ff_2_qn), .preset(and_34_out),
    .reset(and_30_out));
  and and_5 (and_5_out, nor_1_out, d_ff_3_q);
  not not_3 (not_3_out, nor_1_out);
  and and_6 (and_6_out, not_3_out, d_ff_1_q);
  and and_7 (and_7_out, nor_3_out, j_k_ff_2_q[0]);
  and and_8 (and_8_out, j_k_ff_2_qn, not_2_out);
  and and_9 (and_9_out, j_k_ff_1_q, in_1);
  and and_10 (and_10_out, j_k_ff_1_qn, in_1);
  or or_3 (or_3_out, and_5_out, and_6_out);
  or or_4 (or_4_out, and_7_out, and_8_out);
  J_K_Flip_Flop j_k_ff_3 (
    .J(1'b1), .K(1'b1), .clk(and_29_out), .Q(j_k_ff_3_q[0]), .Qn(j_k_ff_3_qn), .reset(and_34_out));  // open: preset
  not not_4 (not_4_out, nor_3_out);
  D_Flip_Flop d_ff_2 (.D(or_3_out), .clk(and_3_out), .Q(d_ff_2_q));  // open: Qn, preset, reset
  and and_11 (and_11_out, in_1, d_ff_2_q);
  LED VOLUME2 (.in(and_11_out));
  J_K_Flip_Flop j_k_ff_4 (
    .J(or_4_out), .K(or_4_out), .clk(buffer_14_out), .Q(j_k_ff_2_q[1]), .Qn(j_k_ff_4_qn), .reset(or_5_out));  // open: preset
  or or_5 (or_5_out, and_30_out, and_31_out);
  LED outputplAY (.in(and_9_out));
  LED outputpause (.in(and_10_out));
  not not_5 (not_5_out, nor_1_out);
  and and_12 (and_12_out, and_7_out, j_k_ff_2_q[1]);
  and and_13 (and_13_out, j_k_ff_4_qn, and_8_out);
  and and_14 (and_14_out, nor_3_out, j_k_ff_3_q[0]);
  and and_15 (and_15_out, j_k_ff_3_qn, not_4_out);
  and and_16 (and_16_out, nor_1_out, d_ff_4_q);
  and and_17 (and_17_out, not_5_out, d_ff_2_q);
  or or_6 (or_6_out, and_12_out, and_13_out);
  J_K_Flip_Flop j_k_ff_5 (
    .J(or_7_out), .K(or_7_out), .clk(and_29_out), .Q(j_k_ff_3_q[1]), .Qn(j_k_ff_5_qn), .reset(or_8_out));  // open: preset
  or or_7 (or_7_out, and_14_out, and_15_out);
  or or_8 (or_8_out, and_34_out, and_37_out);
  D_Flip_Flop d_ff_3 (.D(or_9_out), .clk(and_3_out), .Q(d_ff_3_q));  // open: Qn, preset, reset
  or or_9 (or_9_out, and_16_out, and_17_out);
  J_K_Flip_Flop j_k_ff_6 (
    .J(or_6_out), .K(or_6_out), .clk(buffer_14_out), .Q(j_k_ff_2_q[2]), .Qn(j_k_ff_6_qn), .reset(or_10_out));  // open: preset
  or or_10 (or_10_out, and_30_out, and_31_out);
  and and_18 (and_18_out, in_1, d_ff_3_q);
  LED VOLUME3 (.in(and_18_out));
  and and_19 (and_19_out, and_14_out, j_k_ff_3_q[1]);
  and and_20 (and_20_out, j_k_ff_5_qn, and_15_out);
  not not_6 (not_6_out, nor_1_out);
  and and_21 (and_21_out, and_12_out, j_k_ff_2_q[2]);
  and and_22 (and_22_out, j_k_ff_6_qn, and_13_out);
  J_K_Flip_Flop j_k_ff_7 (
    .J(or_11_out), .K(or_11_out), .clk(and_29_out), .Q(j_k_ff_3_q[2]), .Qn(j_k_ff_7_qn), .reset(or_13_out));  // open: preset
  or or_11 (or_11_out, and_19_out, and_20_out);
  and and_23 (and_23_out, nor_1_out, d_ff_5_q);
  and and_24 (and_24_out, not_6_out, d_ff_3_q);
  J_K_Flip_Flop j_k_ff_8 (
    .J(or_12_out), .K(or_12_out), .clk(buffer_14_out), .Q(j_k_ff_2_q[3]), .reset(and_30_out));  // open: Qn, preset
  or or_12 (or_12_out, and_21_out, and_22_out);
  or or_13 (or_13_out, and_34_out, and_37_out);
  D_Flip_Flop d_ff_4 (.D(or_14_out), .clk(and_3_out), .Q(d_ff_4_q));  // open: Qn, preset, reset
  or or_14 (or_14_out, and_23_out, and_24_out);
  and and_25 (and_25_out, and_19_out, j_k_ff_3_q[2]);
  and and_26 (and_26_out, j_k_ff_7_qn, and_20_out);
  and and_27 (and_27_out, in_1, d_ff_4_q);
  LED VOLUME4 (.in(and_27_out));
  not not_7 (not_7_out, j_k_ff_2_q[0]);
  not not_8 (not_8_out, j_k_ff_2_q[2]);
  and and_28 (and_28_out, not_9_out, not_11_out);
  not not_9 (not_9_out, j_k_ff_2_q[0]);
  or or_15 (or_15_out, and_25_out, and_26_out);
  not not_10 (not_10_out, nor_1_out);
  and and_29 (and_29_out, not_7_out, j_k_ff_2_q[1], not_8_out, j_k_ff_2_q[3]);
  and and_30 (and_30_out, and_28_out, and_31_out);
  and and_31 (and_31_out, buffer_17_out, buffer_18_out);
  not not_11 (not_11_out, j_k_ff_2_q[2]);
  buf buffer_17 (buffer_17_out, j_k_ff_2_q[1]);
  J_K_Flip_Flop j_k_ff_9 (
    .J(or_15_out), .K(or_15_out), .clk(and_29_out), .Q(j_k_ff_3_q[3]), .reset(and_34_out));  // open: Qn, preset
  and and_32 (and_32_out, nor_1_out, d_ff_6_q);
  and and_33 (and_33_out, not_10_out, d_ff_4_q);
  buf buffer_18 (buffer_18_out, j_k_ff_2_q[3]);
  not not_12 (not_12_out, j_k_ff_3_q[0]);
  D_Flip_Flop d_ff_5 (.D(or_16_out), .clk(and_3_out), .Q(d_ff_5_q));  // open: Qn, preset, reset
  or or_16 (or_16_out, and_32_out, and_33_out);
  and and_34 (and_34_out, and_35_out, and_37_out);
  and and_35 (and_35_out, not_12_out, not_13_out);
  not not_13 (not_13_out, j_k_ff_3_q[2]);
  buf buffer_19 (buffer_19_out, j_k_ff_3_q[1]);
  and and_36 (and_36_out, in_1, d_ff_5_q);
  LED VOLUME5 (.in(and_36_out));
  and and_37 (and_37_out, buffer_19_out, buffer_20_out);
  buf buffer_20 (buffer_20_out, j_k_ff_3_q[3]);
  not not_14 (not_14_out, nor_1_out);
  and and_38 (and_38_out, not_14_out, d_ff_5_q);
  assign and_39_out = j_k_ff_2_q & {4{in_1}};  // AND_Gate and_39, 4 bits wide
  and and_40 (and_40_out, nor_1_out, d_ff_7_q);
  or or_17 (or_17_out, and_40_out, and_38_out);
  D_Flip_Flop d_ff_6 (.D(or_17_out), .clk(and_3_out), .Q(d_ff_6_q));  // open: Qn, preset, reset
  Hex_Digit_Display hex_digit_display_1 (.value(and_39_out));  // open: dp
  Hex_Digit_Display hex_digit_display_2 (.value(and_41_out));  // open: dp
  assign and_41_out = j_k_ff_3_q & {4{in_1}};  // AND_Gate and_41, 4 bits wide
  and and_42 (and_42_out, in_1, d_ff_6_q);
  LED VOLUME6 (.in(and_42_out));
  not not_15 (not_15_out, nor_1_out);
  and and_43 (and_43_out, not_15_out, d_ff_6_q);
  and and_44 (and_44_out, nor_1_out, d_ff_8_q);
  or or_18 (or_18_out, and_44_out, and_43_out);
  D_Flip_Flop d_ff_7 (.D(or_18_out), .clk(and_3_out), .Q(d_ff_7_q));  // open: Qn, preset, reset
  and and_45 (and_45_out, in_1, d_ff_7_q);
  LED VOLUME7 (.in(and_45_out));
  not not_16 (not_16_out, nor_1_out);
  and and_46 (and_46_out, nor_1_out, in_2);
  and and_47 (and_47_out, not_16_out, d_ff_7_q);
  or or_19 (or_19_out, and_46_out, and_47_out);
  D_Flip_Flop d_ff_8 (.D(or_19_out), .clk(and_3_out), .Q(d_ff_8_q));  // open: Qn, preset, reset
  and and_48 (and_48_out, in_1, d_ff_8_q);
  LED VOLUME8 (.in(and_48_out));
endmodule
